# Fritzing sketch timer-sense-light-1 (saved by Fritzing 0.9.2b)
breadboards: 1

parts:
  Raspberry_Pi1 = Raspberry Pi B+
  PIR1 = PIR sensor

nets:
  N1: Raspberry_Pi1.GPIO17, PIR1.SIG
  GND: Raspberry_Pi1.GND, PIR1.GND
  5V: Raspberry_Pi1.5V, PIR1.VDD
