# Fritzing sketch timer-sense-light-1 (saved by Fritzing 0.9.2b)
breadboards: 1

parts:
  PIR1 = PIR sensor
  Raspberry_Pi1 = Raspberry Pi B rev2

nets:
  VDD: PIR1.VDD, Raspberry_Pi1.5V
  N1: PIR1.SIG, Raspberry_Pi1.GPIO_17
  GND: PIR1.GND, Raspberry_Pi1.GND
