# Fritzing sketch sense-light-3 (saved by Fritzing 0.9.2b)
breadboards: 1

parts:
  Raspberry_Pi1 = Raspberry Pi B+
  R3 = Resistor [tolerance=±5% resistance=270 package=THT]
  R4 = Resistor [tolerance=±5% resistance=270 package=THT]
  LED3 = LED - 5mm [color="Red (633nm)" package="5 mm [THT]"]
  LED4 = LED - 5mm [color="Red (633nm)" package="5 mm [THT]"]
  LED5 = LED - 5mm [color="Red (633nm)" package="5 mm [THT]"]
  LED6 = LED - 5mm [color="Red (633nm)" package="5 mm [THT]"]
  R5 = Resistor [tolerance=±5% resistance=270 package=THT]
  R6 = Resistor [tolerance=±5% resistance=270 package=THT]

nets:
  N1: Raspberry_Pi1.GPIO27, R4.Pin_1
  N2: Raspberry_Pi1.GPIO22, R5.Pin_1
  N3: Raspberry_Pi1.GPIO23, R6.Pin_1
  N4: Raspberry_Pi1.GND, LED3.cathode, LED4.cathode, LED5.cathode, LED6.cathode
  N5: Raspberry_Pi1.GPIO18, R3.Pin_1
  N6: R3.Pin_0, LED3.anode
  N7: R4.Pin_0, LED4.anode
  N8: LED5.anode, R5.Pin_0
  N9: LED6.anode, R6.Pin_0

notes:
  GPIO 2
  GPIO 1
  Ground
  GPIO 3
  GPIO 4
