# Fritzing sketch sense-light-4 (saved by Fritzing 0.9.2b)

parts:
  R2 = Resistor [tolerance=±5% resistance=270 package=THT]
  LED1 = LED - 5mm [color="Red (633nm)" package="5 mm [THT]"]
  LED2 = LED - 5mm [color="Red (633nm)" package="5 mm [THT]"]
  R1 = Resistor [tolerance=±5% resistance=270 package="2512 [SMD]"]
  R3 = Resistor [tolerance=±5% resistance=270 package=THT]
  LED3 = LED - 5mm [color="Red (633nm)" package="5 mm [THT]"]
  R4 = Resistor [tolerance=±5% resistance=270 package=THT]
  LED4 = LED - 5mm [color="Red (633nm)" package="5 mm [THT]"]

nets:
  N1: R2.Pin_0, LED2.anode
  N2: LED1.cathode, LED2.cathode, LED4.cathode
  N3: LED1.anode, R1.Pin_0
  N4: R3.Pin_0, LED3.anode
  N5: R4.Pin_0, LED4.anode

notes:
  Pin12, GPIO 1
  Pin13, GPIO 2
  Pin14, Ground
  Pin15, GPIO 3
  Pin16, GPIO 4
