# Fritzing sketch sense-light-3 (saved by Fritzing 0.9.2b)
breadboards: 1

parts:
  R3 = Resistor [tolerance=±5% resistance=270 package=THT]
  R4 = Resistor [tolerance=±5% resistance=270 package=THT]
  LED3 = LED - 5mm [color="Red (633nm)" package="5 mm [THT]"]
  LED4 = LED - 5mm [color="Red (633nm)" package="5 mm [THT]"]
  LED5 = LED - 5mm [color="Red (633nm)" package="5 mm [THT]"]
  LED6 = LED - 5mm [color="Red (633nm)" package="5 mm [THT]"]
  R5 = Resistor [tolerance=±5% resistance=270 package=THT]
  R6 = Resistor [tolerance=±5% resistance=270 package=THT]
  Raspberry_Pi2 = Raspberry Pi B rev2

nets:
  N1: R3.Pin_0, LED3.anode
  N2: R3.Pin_1, Raspberry_Pi2.GPIO_18
  N3: R4.Pin_0, LED4.anode
  N4: R4.Pin_1, Raspberry_Pi2.GPIO_27
  N5: LED3.cathode, LED4.cathode, LED5.cathode, LED6.cathode, Raspberry_Pi2.GND
  N6: LED5.anode, R5.Pin_0
  N7: LED6.anode, R6.Pin_0
  N8: R5.Pin_1, Raspberry_Pi2.GPIO_22
  N9: R6.Pin_1, Raspberry_Pi2.GPIO_23

notes:
  GPIO 2
  GPIO 1
  Ground
  GPIO 3
  GPIO 4
