# Fritzing sketch ds1302-model-b (saved by Fritzing 0.9.2b)
breadboards: 1

parts:
  Raspberry_Pi1 = Raspberry Pi B rev2
  PCB2 = RTC_DS1302_module
  R1 = Resistor [tolerance=±5% resistance=10k package="0603 [SMD]"]

nets:
  3V3: Raspberry_Pi1.3V3, PCB2.VCC, R1.Pin_0
  N1: Raspberry_Pi1.GPIO_2, PCB2.DAT, R1.Pin_1
  GND: Raspberry_Pi1.GND, PCB2.GND
  N2: Raspberry_Pi1.GPIO_11, PCB2.CLK
  N3: Raspberry_Pi1.GPIO_8, PCB2.RST

notes:
  10K

custom parts:
  RTC_DS1302_module: Arduino module DS1302 SPI Real Time Clock
